// Logisim project project.circ as structural Verilog: 14 circuits, main circuit Project
module Project (
);

  wire alu, branch, Clock, comparison, controlled_buffer_1_out, dataMemRead, dataMemWrite, enableJump,
       enablePC, enableWrite, jump, multiplexer_1_out, multiplexer_4_out, nextInst, or_1_out, or_2_out,
       regWrite, Reset;
  wire [1:0] ALUcontrol;
  wire [3:0] DEST_SRC_OP1, multiplexer_2_out, SRC1_OP2, SRC2;
  wire [9:0] LD_ST_Address;
  wire [17:0] ALUresult, dataMemResult, JumpAddress, multiplexer_3_out, program_counter_1_output, REG1_data,
       REG2_data, REG2_data_new, rom_1_data;

  or or_1 (or_1_out, nextInst, enableJump);
  Button button_1 (.out(Reset));
  Clock clock_1 (.out(Clock));
  Multiplexer #(.enable("false")) multiplexer_1 (.in0(1'b0), .in1(Clock), .out(multiplexer_1_out), .sel(or_1_out));
  Program_Counter program_counter_1 (
    .enableJump(enableJump), .branch(branch), .reset(Reset), .JumpAddress(JumpAddress),
    .BranchAddress(REG2_data_new), .\output (program_counter_1_output), .clock(controlled_buffer_1_out),
    .next(nextInst));
  assign controlled_buffer_1_out = enablePC ? multiplexer_1_out : 1'bz;  // Controlled_Buffer controlled_buffer_1
  ALU alu_1 (
    .Data_1(REG1_data), .Data_2(REG2_data_new), .ALU_Result(ALUresult), .ALUcontrol(ALUcontrol));  // open: out_4
  ROM #(.addrWidth(18), .dataWidth(18)) rom_1 (.addr(program_counter_1_output), .data(rom_1_data));  // open: sel
  Multiplexer #(.width(4), .enable("false")) multiplexer_2 (
    .in0(SRC2), .in1(DEST_SRC_OP1), .out(multiplexer_2_out), .sel(or_2_out));
  or or_2 (or_2_out, dataMemWrite, comparison);
  Control_Unit control_unit_1 (
    .Instruction(rom_1_data), .Register_1(REG1_data), .Register_2(REG2_data), .ALUcontrol(ALUcontrol),
    .SRC2(SRC2), .regWrite(regWrite), .SRC1_OP2(SRC1_OP2), .DEST_SRC_OP1(DEST_SRC_OP1),
    .dataMemRead(dataMemRead), .dataMemWrite(dataMemWrite), .jump(jump), .branch(branch),
    .REG2_data_new(REG2_data_new), .LD_ST_ADDRESS(LD_ST_Address), .JumpAddress(JumpAddress),
    .comparison(comparison), .alu(alu));
  Multiplexer #(.width(18), .enable("false")) multiplexer_3 (
    .in0(ALUresult), .in1(dataMemResult), .out(multiplexer_3_out), .sel(dataMemRead));
  Register_File register_file_1 (
    .Write_Data(multiplexer_3_out), .Clock(Clock), .Enable_Write(multiplexer_4_out),
    .Read_Register_1(SRC1_OP2), .Read_Register_2(multiplexer_2_out), .Read_Data_1(REG1_data),
    .Read_Data_2(REG2_data), .Write_Address(DEST_SRC_OP1));
  Multiplexer #(.enable("false")) multiplexer_4 (
    .in0(1'b0), .in1(regWrite), .out(multiplexer_4_out), .sel(enableWrite));
  RAM #(.addrWidth(10), .dataWidth(18), .bus("separate")) ram_1 (
    .addr(LD_ST_Address), .din(REG2_data_new), .data(dataMemResult), .str(dataMemWrite), .sel(1'b1),
    .clk(Clock), .ld(dataMemRead));  // open: clr
  FSM fsm_1 (
    .clock(Clock), .LD(dataMemRead), .ST(dataMemWrite), .jump(jump), .comparison(comparison), .alu(alu),
    .enableWrite(enableWrite), .enablePC(enablePC), .nextInst(nextInst), .enableJump(enableJump));

  // Notes on the sheet:
  //   contents of rom_1 (hex, n*v repeats v):
  //   10443 108be 5448 9848 884 204c 1c4c 24802 21002 28002 d848 2d0ba
  //   Check if ST or comparison
endmodule

module Register_File (
  input  [3:0] Write_Address,
  input  [17:0] Write_Data,
  input  Clock,
  input  Enable_Write,
  input  [3:0] Read_Register_1,
  input  [3:0] Read_Register_2,
  output [17:0] Read_Data_1,
  output [17:0] Read_Data_2
);

  wire _0, _1, _2, _3, _4, _5, _6, _7, _8, _9, _10, _11, _12, _13, _14, _15, and_1_out, and_2_out, and_3_out,
       and_4_out, and_5_out, and_6_out, and_7_out, and_8_out, and_9_out, and_10_out, and_11_out, and_12_out,
       and_13_out, and_14_out, and_15_out, and_16_out;
  wire [17:0] Q0, Q1, Q2, Q3, Q4, Q5, Q6, Q7, Q8, Q9, Q10, Q11, Q12, Q13, Q14, Q15;

  Decoder #(.select(4), .enable("false")) decoder_1 (
    .out0(_0), .out1(_1), .out2(_2), .out3(_3), .out4(_4), .out5(_5), .out6(_6), .out7(_7), .out8(_8),
    .out9(_9), .out10(_10), .out11(_11), .out12(_12), .out13(_13), .out14(_14), .out15(_15),
    .sel(Write_Address));
  and and_1 (and_1_out, _0, Enable_Write);
  and and_2 (and_2_out, _1, Enable_Write);
  and and_3 (and_3_out, _2, Enable_Write);
  and and_4 (and_4_out, _3, Enable_Write);
  and and_5 (and_5_out, _4, Enable_Write);
  and and_6 (and_6_out, _5, Enable_Write);
  and and_7 (and_7_out, _6, Enable_Write);
  and and_8 (and_8_out, _7, Enable_Write);
  Register #(.width(18)) register_1 (.D(Write_Data), .en(and_1_out), .Q(Q0), .clk(Clock));  // open: clr
  Register #(.width(18)) register_2 (.D(Write_Data), .en(and_2_out), .Q(Q1), .clk(Clock));  // open: clr
  Register #(.width(18)) register_3 (.D(Write_Data), .en(and_3_out), .Q(Q2), .clk(Clock));  // open: clr
  Register #(.width(18)) register_4 (.D(Write_Data), .en(and_4_out), .Q(Q3), .clk(Clock));  // open: clr
  Register #(.width(18)) register_5 (.D(Write_Data), .en(and_5_out), .Q(Q4), .clk(Clock));  // open: clr
  Register #(.width(18)) register_6 (.D(Write_Data), .en(and_6_out), .Q(Q5), .clk(Clock));  // open: clr
  Register #(.width(18)) register_7 (.D(Write_Data), .en(and_7_out), .Q(Q6), .clk(Clock));  // open: clr
  Register #(.width(18)) register_8 (.D(Write_Data), .en(and_8_out), .Q(Q7), .clk(Clock));  // open: clr
  and and_9 (and_9_out, _8, Enable_Write);
  and and_10 (and_10_out, _9, Enable_Write);
  and and_11 (and_11_out, _10, Enable_Write);
  and and_12 (and_12_out, _11, Enable_Write);
  and and_13 (and_13_out, _12, Enable_Write);
  and and_14 (and_14_out, _13, Enable_Write);
  and and_15 (and_15_out, _14, Enable_Write);
  and and_16 (and_16_out, _15, Enable_Write);
  Register #(.width(18)) register_9 (.D(Write_Data), .en(and_9_out), .Q(Q8), .clk(Clock));  // open: clr
  Register #(.width(18)) register_10 (.D(Write_Data), .en(and_10_out), .Q(Q9), .clk(Clock));  // open: clr
  Register #(.width(18)) register_11 (.D(Write_Data), .en(and_11_out), .Q(Q10), .clk(Clock));  // open: clr
  Register #(.width(18)) register_12 (.D(Write_Data), .en(and_12_out), .Q(Q11), .clk(Clock));  // open: clr
  Register #(.width(18)) register_13 (.D(Write_Data), .en(and_13_out), .Q(Q12), .clk(Clock));  // open: clr
  Register #(.width(18)) register_14 (.D(Write_Data), .en(and_14_out), .Q(Q13), .clk(Clock));  // open: clr
  Register #(.width(18)) register_15 (.D(Write_Data), .en(and_15_out), .Q(Q14), .clk(Clock));  // open: clr
  Register #(.width(18)) register_16 (.D(Write_Data), .en(and_16_out), .Q(Q15), .clk(Clock));  // open: clr
  Multiplexer #(.select(4), .width(18), .enable("false")) multiplexer_1 (
    .in0(Q0), .in1(Q1), .in2(Q2), .in3(Q3), .in4(Q4), .in5(Q5), .in6(Q6), .in7(Q7), .in8(Q8), .in9(Q9),
    .in10(Q10), .in11(Q11), .in12(Q12), .in13(Q13), .in14(Q14), .in15(Q15), .out(Read_Data_1),
    .sel(Read_Register_1));
  Multiplexer #(.select(4), .width(18), .enable("false")) multiplexer_2 (
    .in0(Q0), .in1(Q1), .in2(Q2), .in3(Q3), .in4(Q4), .in5(Q5), .in6(Q6), .in7(Q7), .in8(Q8), .in9(Q9),
    .in10(Q10), .in11(Q11), .in12(Q12), .in13(Q13), .in14(Q14), .in15(Q15), .out(Read_Data_2),
    .sel(Read_Register_2));

  // Other names for the same wires on the sheet: C = Clock; R1[3:0] = Read_Register_1; R2[3:0] = Read_Register_2;
  //   RW = Enable_Write; WD[17:0] = Write_Data

  // Notes on the sheet:
  //   Decode write address
  //   Register File
endmodule

module Control_Unit (
  input  [17:0] Instruction,
  input  [17:0] Register_1,
  input  [17:0] Register_2,
  output [17:0] JumpAddress,
  output [9:0] LD_ST_ADDRESS,
  output [1:0] ALUcontrol,
  output alu,
  output regWrite,
  output [3:0] SRC2,
  output [3:0] SRC1_OP2,
  output [3:0] DEST_SRC_OP1,
  output comparison,
  output dataMemRead,
  output dataMemWrite,
  output branch,
  output jump,
  output [17:0] REG2_data_new
);

  wire ADD, ADDI, AND, and_1_out, and_2_out, and_3_out, and_4_out, and_5_out, ANDI, BEQ, BGE, BGT, BLE, BLT,
       compare_18bits_1_equal, compare_18bits_1_greater, compare_18bits_1_lessthan, immediate, OR, or_1_out,
       or_2_out, or_3_out, or_4_out, or_5_out, or_8_out, ORI, XOR, XORI;
  wire [17:0] sign_extend_6_18_1_output;

  Decoder #(.select(4), .enable("false")) decoder_1 (
    .out0(ADD), .out1(AND), .out2(OR), .out3(XOR), .out4(ADDI), .out5(ANDI), .out6(ORI), .out7(XORI),
    .out8(dataMemRead), .out9(dataMemWrite), .out10(jump), .out11(BEQ), .out12(BLT), .out13(BGT),
    .out14(BLE), .out15(BGE), .sel(Instruction[17:14]));
  Sign_Extend_14_18 sign_extend_14_18_1 (.\input (Instruction[13:0]), .\output (JumpAddress));
  Compare_18bits compare_18bits_1 (
    .a(Register_2), .b(Register_1), .Greater(compare_18bits_1_greater), .LessThan(compare_18bits_1_lessthan),
    .Equal(compare_18bits_1_equal));
  or or_1 (or_1_out, AND, ANDI);
  or or_2 (or_2_out, OR, ORI);
  or or_3 (or_3_out, XOR, XORI);
  or or_4 (or_4_out, compare_18bits_1_equal, compare_18bits_1_greater);
  or or_5 (or_5_out, compare_18bits_1_lessthan, compare_18bits_1_equal);
  Sign_Extend_6_18 sign_extend_6_18_1 (.\input (Instruction[5:0]), .\output (sign_extend_6_18_1_output));
  or or_6 (ALUcontrol[0], or_2_out, or_3_out);
  or or_7 (ALUcontrol[1], or_1_out, or_3_out);
  and and_1 (and_1_out, or_4_out, BGE);
  and and_2 (and_2_out, BGT, compare_18bits_1_greater);
  and and_3 (and_3_out, BEQ, compare_18bits_1_equal);
  and and_4 (and_4_out, BLT, compare_18bits_1_lessthan);
  and and_5 (and_5_out, BLE, or_5_out);
  Multiplexer #(.width(18), .enable("false")) multiplexer_1 (
    .in0(Register_2), .in1(sign_extend_6_18_1_output), .out(REG2_data_new), .sel(or_8_out));
  or or_8 (or_8_out, immediate, comparison);
  or or_9 (immediate, ANDI, ORI, XORI, ADDI);
  or or_10 (branch, and_1_out, and_2_out, and_3_out, and_4_out, and_5_out);
  or or_11 (alu, ADD, AND, OR, XOR, ADDI, ANDI, ORI, XORI);
  or or_12 (comparison, BEQ, BLT, BGT, BLE, BGE);
  or or_13 (regWrite, alu, dataMemRead);

  assign DEST_SRC_OP1 = Instruction[13:10];
  assign LD_ST_ADDRESS = Instruction[9:0];
  assign SRC1_OP2 = Instruction[9:6];
  assign SRC2 = Instruction[5:2];

  // Other names for the same wires on the sheet: IMMEDIATE_BRANCH_Address[5:0] = Instruction[5:0]; LD = dataMemRead;
  //   ST = dataMemWrite

  // Notes on the sheet:
  //   Decode Opeartion
  //   Decode addresses and SRC/DEST/OP
  //   Compare 2 registers and branch according to result
  //   Choose ALU operation
  //   ADD/ADDI 00 - AND/ANDI 10 - ORR/ORRI 01 - XOR/XORI 11
  //   Choose register_2 data or immediate data
  //   Check if any immediate value exist
  //   any writing to register exists
endmodule

module ALU (
  input  [17:0] Data_1,
  input  [17:0] Data_2,
  input  [1:0] ALUcontrol,
  output out_4,
  output [17:0] ALU_Result
);

  wire [17:0] and_1_out, n18bit_adder_1_sum, or_1_out, xor_1_out;

  _18bit_adder u_18bit_adder_1 (.A(Data_1), .B(Data_2), .carry_in(1'b0), .carry_out(out_4), .sum(n18bit_adder_1_sum));
  assign or_1_out = Data_1 | Data_2;  // OR_Gate or_1, 18 bits wide
  assign and_1_out = Data_1 & Data_2;  // AND_Gate and_1, 18 bits wide
  assign xor_1_out = Data_1 ^ Data_2;  // XOR_Gate xor_1, 18 bits wide
  Multiplexer #(.select(2), .width(18), .enable("false")) multiplexer_1 (
    .in0(n18bit_adder_1_sum), .in1(or_1_out), .in2(and_1_out), .in3(xor_1_out), .out(ALU_Result),
    .sel(ALUcontrol));
endmodule

module Program_Counter (
  input  next,
  input  enableJump,
  input  branch,
  input  clock,
  input  reset,
  input  [17:0] JumpAddress,
  input  [17:0] BranchAddress,
  output [17:0] \output 
);

  wire and_1_out, not_1_out, or_1_out;
  wire [17:0] multiplexer_1_out, result;

  not not_1 (not_1_out, next);
  and and_1 (and_1_out, not_1_out, or_1_out);
  or or_1 (or_1_out, enableJump, branch);
  Counter #(.width(18), .max('h3ffff)) counter_1 (
    .load(and_1_out), .D(result), .count(next), .Q(\output ), .clk(clock), .clr(reset));  // open: carry
  Multiplexer #(.width(18)) multiplexer_1 (
    .in0(JumpAddress), .in1(BranchAddress), .out(multiplexer_1_out), .sel(branch), .en(enableJump));
  _18bit_adder u_18bit_adder_1 (.A(\output ), .B(multiplexer_1_out), .carry_in(1'b0), .sum(result));  // open: carry_out
endmodule

module FSM (
  input  clock,
  input  LD,
  input  ST,
  input  jump,
  input  comparison,
  input  alu,
  output enableWrite,
  output enablePC,
  output nextInst,
  output enableJump
);

  wire alu_pc, alu_wr, branch_pc, controlled_buffer_1_out, controlled_buffer_2_out, controlled_buffer_3_out,
       controlled_buffer_4_out, controlled_buffer_5_out, counter_3_q, decoder_1_out0, decoder_1_out2,
       decoder_2_out0, decoder_2_out2, decoder_3_out0, decoder_3_out1, decoder_4_out1, decoder_4_out2,
       decoder_5_out1, decoder_5_out3, jump_pc, ld_pc, ld_wr, st_pc;
  wire [1:0] counter_1_q, counter_2_q, counter_4_q, counter_5_q;

  Counter #(.width(2), .max('h2)) counter_1 (
    .Q(counter_1_q), .clk(controlled_buffer_1_out));  // open: load, D, count, carry, clr
  assign controlled_buffer_1_out = alu ? clock : 1'bz;  // Controlled_Buffer controlled_buffer_1
  assign controlled_buffer_2_out = LD ? clock : 1'bz;  // Controlled_Buffer controlled_buffer_2
  assign controlled_buffer_3_out = ST ? clock : 1'bz;  // Controlled_Buffer controlled_buffer_3
  assign controlled_buffer_4_out = comparison ? clock : 1'bz;  // Controlled_Buffer controlled_buffer_4
  Counter #(.width(2), .max('h2)) counter_2 (
    .Q(counter_2_q), .clk(controlled_buffer_2_out));  // open: load, D, count, carry, clr
  Counter #(.width(1), .max('h1)) counter_3 (
    .Q(counter_3_q), .clk(controlled_buffer_3_out));  // open: load, D, count, carry, clr
  Counter #(.width(2), .max('h2)) counter_4 (
    .Q(counter_4_q), .clk(controlled_buffer_4_out));  // open: load, D, count, carry, clr
  Counter #(.width(2), .max('h2)) counter_5 (
    .Q(counter_5_q), .clk(controlled_buffer_5_out));  // open: load, D, count, carry, clr
  assign controlled_buffer_5_out = jump ? clock : 1'bz;  // Controlled_Buffer controlled_buffer_5
  assign alu_pc = decoder_1_out0 ? 1'b0 : 1'bz;  // Controlled_Buffer controlled_buffer_6
  Decoder #(.select(2), .enable("false")) decoder_1 (
    .out0(decoder_1_out0), .out1(alu_wr), .out2(decoder_1_out2), .sel(counter_1_q));  // open: out3
  assign alu_pc = decoder_1_out2 ? 1'b1 : 1'bz;  // Controlled_Buffer controlled_buffer_7
  assign ld_pc = decoder_2_out0 ? 1'b0 : 1'bz;  // Controlled_Buffer controlled_buffer_8
  Decoder #(.select(2), .enable("false")) decoder_2 (
    .out0(decoder_2_out0), .out1(ld_wr), .out2(decoder_2_out2), .sel(counter_2_q));  // open: out3
  Decoder #(.enable("false")) decoder_3 (.out0(decoder_3_out0), .out1(decoder_3_out1), .sel(counter_3_q));
  Decoder #(.select(2), .enable("false")) decoder_4 (
    .out1(decoder_4_out1), .out2(decoder_4_out2), .sel(counter_4_q));  // open: out0, out3
  Decoder #(.select(2), .enable("false")) decoder_5 (
    .out1(decoder_5_out1), .out3(decoder_5_out3), .sel(counter_5_q));  // open: out0, out2
  assign ld_pc = decoder_2_out2 ? 1'b1 : 1'bz;  // Controlled_Buffer controlled_buffer_9
  assign st_pc = decoder_3_out0 ? 1'b0 : 1'bz;  // Controlled_Buffer controlled_buffer_10
  assign st_pc = decoder_3_out1 ? 1'b1 : 1'bz;  // Controlled_Buffer controlled_buffer_11
  assign branch_pc = decoder_4_out1 ? 1'b1 : 1'bz;  // Controlled_Buffer controlled_buffer_12
  assign branch_pc = decoder_4_out2 ? 1'b0 : 1'bz;  // Controlled_Buffer controlled_buffer_13
  assign jump_pc = decoder_5_out1 ? 1'b1 : 1'bz;  // Controlled_Buffer controlled_buffer_14
  assign jump_pc = decoder_5_out3 ? 1'b0 : 1'bz;  // Controlled_Buffer controlled_buffer_15
  or or_1 (enableWrite, alu_wr, ld_wr);
  or or_2 (enablePC, alu_pc, ld_pc, st_pc, branch_pc, jump_pc);
  or or_3 (nextInst, alu_pc, ld_pc, st_pc);
  or or_4 (enableJump, branch_pc, branch_pc, jump_pc, jump_pc);

  // Notes on the sheet:
  //   ALU
  //   LD
  //   ST
  //   Branch
  //   Jump
endmodule

module Sign_Extend_14_18 (
  input  [13:0] \input ,
  output [17:0] \output 
);

  Multiplexer #(.width(4), .enable("false")) multiplexer_1 (
    .in0(4'b0000), .in1(4'b1111), .out(\output [17:14]), .sel(\input [13]));

  assign \output [13:0] = \input ;
endmodule

module Sign_Extend_6_18 (
  input  [5:0] \input ,
  output [17:0] \output 
);

  Multiplexer #(.width(12), .enable("false")) multiplexer_1 (
    .in0({12{1'b0}}), .in1({12{1'b1}}), .out(\output [17:6]), .sel(\input [5]));

  assign \output [5:0] = \input ;
endmodule

module Compare_18bits (
  input  [17:0] a,
  input  [17:0] b,
  output Greater,
  output LessThan,
  output Equal
);

  wire compare_2bits_1_eq, compare_2bits_1_gt, compare_2bits_1_lt, compare_3bits_1_eq, compare_3bits_1_gt,
       compare_3bits_1_lt, compare_3bits_2_eq, compare_3bits_2_gt, compare_3bits_2_lt, compare_3bits_3_eq,
       compare_3bits_3_gt, compare_3bits_3_lt, compare_3bits_4_eq, compare_3bits_4_gt, compare_3bits_4_lt,
       compare_3bits_5_eq, compare_3bits_5_gt, compare_3bits_5_lt, compare_3bits_6_eq, compare_3bits_6_gt,
       compare_3bits_6_lt, compare_3bits_7_eq, compare_3bits_7_gt, compare_3bits_7_lt, compare_3bits_8_eq,
       compare_3bits_8_gt, compare_3bits_8_lt, compare_3bits_9_eq, compare_3bits_9_gt, compare_3bits_9_lt,
       compare_3bits_10_eq, compare_3bits_10_gt, compare_3bits_10_lt, compare_3bits_11_eq,
       compare_3bits_11_gt, compare_3bits_11_lt, compare_3bits_12_eq, compare_3bits_12_gt,
       compare_3bits_12_lt, compare_3bits_13_eq, compare_3bits_13_gt, compare_3bits_13_lt,
       compare_3bits_14_eq, compare_3bits_14_gt, compare_3bits_14_lt, compare_3bits_15_eq,
       compare_3bits_15_gt, compare_3bits_15_lt, compare_3bits_16_eq, compare_3bits_16_gt,
       compare_3bits_16_lt;

  Compare_2bits compare_2bits_1 (
    .A(a[17]), .B(b[17]), .gt(compare_2bits_1_gt), .lt(compare_2bits_1_lt), .eq(compare_2bits_1_eq));
  Compare_3bits compare_3bits_1 (
    .a(a[8]), .b(b[8]), .gt_in(compare_3bits_16_gt), .lt_in(compare_3bits_16_lt),
    .eq_in(compare_3bits_16_eq), .gt(compare_3bits_1_gt), .lt(compare_3bits_1_lt), .eq(compare_3bits_1_eq));
  Compare_3bits compare_3bits_2 (
    .a(a[16]), .b(b[16]), .gt_in(compare_2bits_1_gt), .lt_in(compare_2bits_1_lt), .eq_in(compare_2bits_1_eq),
    .gt(compare_3bits_2_gt), .lt(compare_3bits_2_lt), .eq(compare_3bits_2_eq));
  Compare_3bits compare_3bits_3 (
    .a(a[7]), .b(b[7]), .gt_in(compare_3bits_1_gt), .lt_in(compare_3bits_1_lt), .eq_in(compare_3bits_1_eq),
    .gt(compare_3bits_3_gt), .lt(compare_3bits_3_lt), .eq(compare_3bits_3_eq));
  Compare_3bits compare_3bits_4 (
    .a(a[15]), .b(b[15]), .gt_in(compare_3bits_2_gt), .lt_in(compare_3bits_2_lt), .eq_in(compare_3bits_2_eq),
    .gt(compare_3bits_4_gt), .lt(compare_3bits_4_lt), .eq(compare_3bits_4_eq));
  Compare_3bits compare_3bits_5 (
    .a(a[14]), .b(b[14]), .gt_in(compare_3bits_4_gt), .lt_in(compare_3bits_4_lt), .eq_in(compare_3bits_4_eq),
    .gt(compare_3bits_5_gt), .lt(compare_3bits_5_lt), .eq(compare_3bits_5_eq));
  Compare_3bits compare_3bits_6 (
    .a(a[6]), .b(b[6]), .gt_in(compare_3bits_3_gt), .lt_in(compare_3bits_3_lt), .eq_in(compare_3bits_3_eq),
    .gt(compare_3bits_6_gt), .lt(compare_3bits_6_lt), .eq(compare_3bits_6_eq));
  Compare_3bits compare_3bits_7 (
    .a(a[13]), .b(b[13]), .gt_in(compare_3bits_5_gt), .lt_in(compare_3bits_5_lt), .eq_in(compare_3bits_5_eq),
    .gt(compare_3bits_7_gt), .lt(compare_3bits_7_lt), .eq(compare_3bits_7_eq));
  Compare_3bits compare_3bits_8 (
    .a(a[5]), .b(b[5]), .gt_in(compare_3bits_6_gt), .lt_in(compare_3bits_6_lt), .eq_in(compare_3bits_6_eq),
    .gt(compare_3bits_8_gt), .lt(compare_3bits_8_lt), .eq(compare_3bits_8_eq));
  Compare_3bits compare_3bits_9 (
    .a(a[12]), .b(b[12]), .gt_in(compare_3bits_7_gt), .lt_in(compare_3bits_7_lt), .eq_in(compare_3bits_7_eq),
    .gt(compare_3bits_9_gt), .lt(compare_3bits_9_lt), .eq(compare_3bits_9_eq));
  Compare_3bits compare_3bits_10 (
    .a(a[4]), .b(b[4]), .gt_in(compare_3bits_8_gt), .lt_in(compare_3bits_8_lt), .eq_in(compare_3bits_8_eq),
    .gt(compare_3bits_10_gt), .lt(compare_3bits_10_lt), .eq(compare_3bits_10_eq));
  Compare_3bits compare_3bits_11 (
    .a(a[11]), .b(b[11]), .gt_in(compare_3bits_9_gt), .lt_in(compare_3bits_9_lt), .eq_in(compare_3bits_9_eq),
    .gt(compare_3bits_11_gt), .lt(compare_3bits_11_lt), .eq(compare_3bits_11_eq));
  Compare_3bits compare_3bits_12 (
    .a(a[3]), .b(b[3]), .gt_in(compare_3bits_10_gt), .lt_in(compare_3bits_10_lt),
    .eq_in(compare_3bits_10_eq), .gt(compare_3bits_12_gt), .lt(compare_3bits_12_lt), .eq(compare_3bits_12_eq));
  Compare_3bits compare_3bits_13 (
    .a(a[10]), .b(b[10]), .gt_in(compare_3bits_11_gt), .lt_in(compare_3bits_11_lt),
    .eq_in(compare_3bits_11_eq), .gt(compare_3bits_13_gt), .lt(compare_3bits_13_lt), .eq(compare_3bits_13_eq));
  Compare_3bits compare_3bits_14 (
    .a(a[2]), .b(b[2]), .gt_in(compare_3bits_12_gt), .lt_in(compare_3bits_12_lt),
    .eq_in(compare_3bits_12_eq), .gt(compare_3bits_14_gt), .lt(compare_3bits_14_lt), .eq(compare_3bits_14_eq));
  Compare_3bits compare_3bits_15 (
    .a(a[1]), .b(b[1]), .gt_in(compare_3bits_14_gt), .lt_in(compare_3bits_14_lt),
    .eq_in(compare_3bits_14_eq), .gt(compare_3bits_15_gt), .lt(compare_3bits_15_lt), .eq(compare_3bits_15_eq));
  Compare_3bits compare_3bits_16 (
    .a(a[9]), .b(b[9]), .gt_in(compare_3bits_13_gt), .lt_in(compare_3bits_13_lt),
    .eq_in(compare_3bits_13_eq), .gt(compare_3bits_16_gt), .lt(compare_3bits_16_lt), .eq(compare_3bits_16_eq));
  Compare_3bits compare_3bits_17 (
    .a(a[0]), .b(b[0]), .gt_in(compare_3bits_15_gt), .lt_in(compare_3bits_15_lt),
    .eq_in(compare_3bits_15_eq), .gt(Greater), .lt(LessThan), .eq(Equal));

  // Other names for the same wires on the sheet: a_0 = a[0]; a_1 = a[1]; a_2 = a[2]; a_3 = a[3]; a_4 = a[4];
  //   a_5 = a[5]; a_6 = a[6]; a_7 = a[7]; a_8 = a[8]; a_9 = a[9]; a_10 = a[10]; a_11 = a[11]; a_12 = a[12];
  //   a_13 = a[13]; a_14 = a[14]; a_15 = a[15]; a_16 = a[16]; a_17 = a[17]; b_0 = b[0]; b_1 = b[1]; b_2 = b[2];
  //   b_3 = b[3]; b_4 = b[4]; b_5 = b[5]; b_6 = b[6]; b_7 = b[7]; b_8 = b[8]; b_9 = b[9]; b_10 = b[10]; b_11 = b[11];
  //   b_12 = b[12]; b_13 = b[13]; b_14 = b[14]; b_15 = b[15]; b_16 = b[16]; b_17 = b[17]
endmodule

module Compare_2bits (
  input  A,
  input  B,
  output gt,
  output lt,
  output eq
);

  wire and_1_out, and_4_out, not_1_out, not_2_out, not_3_out, not_4_out;

  not not_1 (not_1_out, A);
  and and_1 (and_1_out, not_1_out, not_2_out);
  not not_2 (not_2_out, B);
  and and_2 (gt, A, not_3_out);
  not not_3 (not_3_out, B);
  not not_4 (not_4_out, A);
  and and_3 (lt, not_4_out, B);
  and and_4 (and_4_out, A, B);
  or or_1 (eq, and_4_out, and_1_out);
endmodule

module Compare_3bits (
  input  a,
  input  b,
  input  gt_in,
  input  lt_in,
  input  eq_in,
  output gt,
  output lt,
  output eq
);

  wire and_1_out, and_2_out, and_3_out, and_4_out, and_5_out, and_6_out, not_1_out, not_2_out, not_3_out,
       not_4_out, or_1_out;

  not not_1 (not_1_out, b);
  not not_2 (not_2_out, a);
  and and_1 (and_1_out, a, b);
  not not_3 (not_3_out, a);
  and and_2 (and_2_out, not_3_out, not_4_out);
  not not_4 (not_4_out, b);
  and and_3 (and_3_out, a, not_1_out);
  and and_4 (and_4_out, and_3_out, eq_in);
  and and_5 (and_5_out, eq_in, and_6_out);
  and and_6 (and_6_out, not_2_out, b);
  or or_1 (or_1_out, and_1_out, and_2_out);
  or or_2 (gt, and_4_out, gt_in);
  or or_3 (lt, and_5_out, lt_in);
  and and_7 (eq, eq_in, or_1_out);
endmodule

module _1bit_adder (
  input  A,
  input  B,
  input  carry_in,
  output sum,
  output carry_out
);

  wire and_1_out, and_2_out, xor_1_out;

  xor xor_1 (xor_1_out, A, B);
  xor xor_2 (sum, xor_1_out, carry_in);
  and and_1 (and_1_out, carry_in, xor_1_out);
  and and_2 (and_2_out, B, A);
  or or_1 (carry_out, and_1_out, and_2_out);
endmodule

module _2bit_adder (
  input  [1:0] A,
  input  [1:0] B,
  input  carry_in,
  output carry_out,
  output [1:0] sum
);

  wire n1bit_adder_1_carry_out;

  _1bit_adder u_1bit_adder_1 (
    .A(A[0]), .B(B[0]), .carry_in(carry_in), .sum(sum[0]), .carry_out(n1bit_adder_1_carry_out));
  _1bit_adder u_1bit_adder_2 (
    .A(A[1]), .B(B[1]), .carry_in(n1bit_adder_1_carry_out), .sum(sum[1]), .carry_out(carry_out));
endmodule

module _18bit_adder (
  input  [17:0] A,
  input  [17:0] B,
  input  carry_in,
  output carry_out,
  output [17:0] sum
);

  wire n2bit_adder_1_carry_out, n2bit_adder_2_carry_out, n2bit_adder_3_carry_out, n2bit_adder_4_carry_out,
       n2bit_adder_5_carry_out, n2bit_adder_6_carry_out, n2bit_adder_7_carry_out, n2bit_adder_8_carry_out;

  _2bit_adder u_2bit_adder_1 (
    .A(A[1:0]), .B(B[1:0]), .carry_in(carry_in), .carry_out(n2bit_adder_1_carry_out), .sum(sum[1:0]));
  _2bit_adder u_2bit_adder_2 (
    .A(A[3:2]), .B(B[3:2]), .carry_in(n2bit_adder_1_carry_out), .carry_out(n2bit_adder_2_carry_out),
    .sum(sum[3:2]));
  _2bit_adder u_2bit_adder_3 (
    .A(A[5:4]), .B(B[5:4]), .carry_in(n2bit_adder_2_carry_out), .carry_out(n2bit_adder_3_carry_out),
    .sum(sum[5:4]));
  _2bit_adder u_2bit_adder_4 (
    .A(A[7:6]), .B(B[7:6]), .carry_in(n2bit_adder_3_carry_out), .carry_out(n2bit_adder_4_carry_out),
    .sum(sum[7:6]));
  _2bit_adder u_2bit_adder_5 (
    .A(A[9:8]), .B(B[9:8]), .carry_in(n2bit_adder_4_carry_out), .carry_out(n2bit_adder_5_carry_out),
    .sum(sum[9:8]));
  _2bit_adder u_2bit_adder_6 (
    .A(A[11:10]), .B(B[11:10]), .carry_in(n2bit_adder_5_carry_out), .carry_out(n2bit_adder_6_carry_out),
    .sum(sum[11:10]));
  _2bit_adder u_2bit_adder_7 (
    .A(A[13:12]), .B(B[13:12]), .carry_in(n2bit_adder_6_carry_out), .carry_out(n2bit_adder_7_carry_out),
    .sum(sum[13:12]));
  _2bit_adder u_2bit_adder_8 (
    .A(A[15:14]), .B(B[15:14]), .carry_in(n2bit_adder_7_carry_out), .carry_out(n2bit_adder_8_carry_out),
    .sum(sum[15:14]));
  _2bit_adder u_2bit_adder_9 (
    .A(A[17:16]), .B(B[17:16]), .carry_in(n2bit_adder_8_carry_out), .carry_out(carry_out), .sum(sum[17:16]));
endmodule
